// Logisim project Fiscsim.circ as structural Verilog: 1 circuit, main circuit main
module main (
);

  wire and_1_out, and_2_out, bit_extender_1_out, CLK, d_ff_1_q, d_ff_1_qn, decoder_1_out0, decoder_1_out1,
       decoder_1_out2, decoder_1_out3, not_1_out;
  wire [3:0] register_5_q, register_5_q_2;
  wire [5:0] adder_1_out, multiplexer_1_out, register_1_q;
  wire [7:0] adder_2_out, and_3_out, multiplexer_2_out, multiplexer_3_out, multiplexer_4_out, nor_1_out,
       not_2_out, register_2_q, register_3_q, register_4_q, rom_1_data;

  Multiplexer #(.width(6)) multiplexer_1 (
    .in0(adder_1_out), .in1(rom_1_data[5:0]), .out(multiplexer_1_out), .sel(and_1_out));
  Adder #(.width(6)) adder_1 (.a(register_1_q), .b(6'b000001), .out(adder_1_out));  // open: cin, cout
  Register #(.width(6)) register_1 (.D(multiplexer_1_out), .clk(CLK), .Q(register_1_q));  // open: en, clr
  Clock clock_1 (.out(CLK));
  ROM #(.addrWidth(6)) rom_1 (.addr(register_1_q), .data(rom_1_data));
  and and_1 (and_1_out, d_ff_1_qn, and_2_out);
  and and_2 (and_2_out, rom_1_data[6], rom_1_data[7]);
  not not_1 (not_1_out, and_2_out);
  Decoder #(.select(2)) decoder_1 (
    .out0(decoder_1_out0), .out1(decoder_1_out1), .out2(decoder_1_out2), .out3(decoder_1_out3),
    .sel(rom_1_data[1:0]), .en(not_1_out));
  D_Flip_Flop d_ff_1 (
    .D(bit_extender_1_out), .clk(CLK), .Q(d_ff_1_q), .Qn(d_ff_1_qn), .reset(not_1_out));  // open: preset
  Register register_2 (.D(multiplexer_4_out), .en(decoder_1_out0), .clk(CLK), .Q(register_2_q));  // open: clr
  Register register_3 (.D(multiplexer_4_out), .en(decoder_1_out1), .clk(CLK), .Q(register_3_q));  // open: clr
  Register register_4 (.D(multiplexer_4_out), .en(decoder_1_out2), .clk(CLK), .Q(register_4_q));  // open: clr
  Register register_5 (
    .D(multiplexer_4_out), .en(decoder_1_out3), .clk(CLK), .Q({register_5_q_2, register_5_q}));  // open: clr
  Bit_Extender #(.out_width(1), .\type ("zero")) bit_extender_1 (.in(nor_1_out), .out(bit_extender_1_out));
  assign nor_1_out = ~(multiplexer_4_out | multiplexer_4_out);  // NOR_Gate nor_1, 8 bits wide
  Multiplexer #(.select(2), .width(8)) multiplexer_2 (
    .in0(register_2_q), .in1(register_3_q), .in2(register_4_q), .in3({register_5_q_2, register_5_q}),
    .out(multiplexer_2_out), .sel(rom_1_data[5:4]));
  Multiplexer #(.select(2), .width(8)) multiplexer_3 (
    .in0(register_2_q), .in1(register_3_q), .in2(register_4_q), .in3({register_5_q_2, register_5_q}),
    .out(multiplexer_3_out), .sel(rom_1_data[3:2]));
  Hex_Digit_Display hex_digit_display_1 (.value(register_5_q_2));  // open: dp
  Hex_Digit_Display hex_digit_display_2 (.value(register_5_q));  // open: dp
  Adder adder_2 (.a(multiplexer_2_out), .b(multiplexer_3_out), .out(adder_2_out));  // open: cin, cout
  assign not_2_out = ~multiplexer_2_out;  // NOT_Gate not_2, 8 bits wide
  assign and_3_out = multiplexer_2_out & multiplexer_3_out;  // AND_Gate and_3, 8 bits wide
  Multiplexer #(.select(2), .width(8)) multiplexer_4 (
    .in0(adder_2_out), .in1(and_3_out), .in2(not_2_out), .in3(not_2_out), .out(multiplexer_4_out),
    .sel(rom_1_data[7:6]));

  // Notes on the sheet:
  //   BNZ
  //   contents of rom_1 (hex, n*v repeats v):
  //   90 44 81 15 91 16 2a 2a 2a 68 2a 2a a 22 22 7c 1f 7d f 54 25 d1 a2 d6
endmodule
