// Logisim project Lab1.Problem1.circ as structural Verilog: 1 circuit, main circuit main
module main (
  input  A,
  input  B,
  input  C,
  input  A_2,
  input  B_2,
  input  C_2,
  input  A_3,
  input  B_3,
  input  C_3
);

  wire not_1_out, not_2_out;

  not not_1 (not_1_out, C_2);
  not not_2 (not_2_out, C_3);
  LED led_1 (.in(C));
  LED led_2 (.in(not_1_out));
  LED led_3 (.in(not_2_out));
  LED led_4 (.in(C_3));

  // Notes on the sheet:
  //   ODD
  //   EVEN
  //   EVEN
  //   ODD
endmodule
