// Logisim project Lab1Problem2.circ as structural Verilog: 1 circuit, main circuit main
module main (
  input  A,
  input  B,
  input  C,
  input  D,
  input  A_2,
  input  B_2,
  input  C_2,
  input  D_2,
  input  A_3,
  input  B_3,
  input  C_3,
  input  D_3
);

  wire and_1_out, and_2_out, and_3_out, not_1_out, not_2_out, not_3_out, not_4_out, not_5_out, not_6_out;

  not not_1 (not_1_out, A);
  not not_2 (not_2_out, B_2);
  not not_3 (not_3_out, A_3);
  not not_4 (not_4_out, B_3);
  not not_5 (not_5_out, C_3);
  not not_6 (not_6_out, D_3);
  and and_1 (and_1_out, not_1_out, B, C);
  and and_2 (and_2_out, A_2, not_2_out);
  and and_3 (and_3_out, not_3_out, not_4_out, not_5_out, not_6_out);
  LED led_1 (.in(and_1_out));
  LED led_2 (.in(and_2_out));
  LED led_3 (.in(and_3_out));
endmodule
