// Logisim project Lab1Problem2NANDGATES.circ as structural Verilog: 1 circuit, main circuit main
module main (
  input  A,
  input  B,
  input  C,
  input  in_4,
  input  D,
  input  in_6,
  input  A_2,
  input  B_2,
  input  C_2,
  input  D_2,
  input  A_3,
  input  B_3,
  input  C_3,
  input  D_3,
  input  A_4,
  input  B_4,
  input  C_4,
  input  D_4
);

  wire nand_1_out, nand_2_out, nand_3_out, nand_4_out, nand_5_out, nand_6_out, nand_7_out, nand_8_out,
       nand_9_out, nand_10_out, nand_11_out, nand_12_out, nand_13_out, nand_14_out, nand_15_out, nand_16_out,
       nand_17_out, nand_18_out, nand_19_out, nand_20_out, nand_21_out, nand_22_out;

  nand nand_1 (nand_1_out, A, A);
  nand nand_2 (nand_2_out, B, B);
  nand nand_3 (nand_3_out, C, C);
  nand nand_4 (nand_4_out, D, D);
  nand nand_5 (nand_5_out, B_2, B_2);
  nand nand_6 (nand_6_out, A_3, A_3);
  nand nand_7 (nand_7_out, A_4, A_4);
  nand nand_8 (nand_8_out, B_4, B_4);
  nand nand_9 (nand_9_out, C_4, C_4);
  nand nand_10 (nand_10_out, D_4, D_4);
  nand nand_11 (nand_11_out, nand_1_out, nand_2_out, nand_3_out, nand_4_out);
  nand nand_12 (nand_12_out, A_2, nand_5_out);
  nand nand_13 (nand_13_out, nand_6_out, B_3, C_3);
  nand nand_14 (nand_14_out, nand_12_out, nand_12_out);
  nand nand_15 (nand_15_out, A_4, nand_8_out);
  nand nand_16 (nand_16_out, nand_7_out, nand_8_out, nand_9_out, nand_10_out);
  nand nand_17 (nand_17_out, nand_7_out, B_4, C_4);
  nand nand_18 (nand_18_out, nand_11_out, nand_11_out);
  nand nand_19 (nand_19_out, nand_13_out, nand_13_out);
  LED led_1 (.in(nand_14_out));
  LED led_2 (.in(nand_19_out));
  nand nand_20 (nand_20_out, nand_15_out, nand_15_out);
  nand nand_21 (nand_21_out, nand_16_out, nand_16_out);
  nand nand_22 (nand_22_out, nand_17_out, nand_17_out);
  LED led_3 (.in(nand_18_out));
  LED led_4 (.in(nand_20_out));
  LED led_5 (.in(nand_21_out));
  LED led_6 (.in(nand_22_out));

  // Notes on the sheet:
  //   <-5
  //   ZERO
  //   >5
  //   <-5
  //   ZERO
  //   >5
endmodule
