// Logisim project Lab1Problem4.circ as structural Verilog: 1 circuit, main circuit main
module main (
  input  A,
  input  B,
  input  C,
  input  D,
  input  A_2,
  input  B_2,
  input  C_2,
  input  D_2,
  input  A_3,
  input  B_3,
  input  C_3,
  input  D_3
);

  wire and_1_out, and_2_out, and_3_out, and_4_out, and_5_out, and_6_out, and_7_out, and_8_out, not_1_out,
       not_2_out, not_3_out, not_4_out, or_1_out, or_2_out, or_3_out, or_4_out;

  and and_1 (and_1_out, B, C);
  not not_1 (not_1_out, B_2);
  not not_2 (not_2_out, C_2);
  not not_3 (not_3_out, B_3);
  not not_4 (not_4_out, C_3);
  or or_1 (or_1_out, A, and_1_out);
  and and_2 (and_2_out, A_2, C_2);
  and and_3 (and_3_out, not_1_out, C_2);
  and and_4 (and_4_out, B_2, not_2_out);
  and and_5 (and_5_out, B_3, C_3);
  and and_6 (and_6_out, A_3, C_3);
  and and_7 (and_7_out, not_3_out, C_3);
  and and_8 (and_8_out, B_3, not_4_out);
  LED led_1 (.in(or_1_out));
  or or_2 (or_2_out, and_2_out, and_3_out, and_4_out);
  or or_3 (or_3_out, and_5_out, A_3);
  or or_4 (or_4_out, and_6_out, and_7_out, and_8_out);
  LED led_2 (.in(or_2_out));
  LED led_3 (.in(or_3_out));
  LED led_4 (.in(or_4_out));

  // Notes on the sheet:
  //   X
  //   Y
  //   X
  //   Y
endmodule
