// Logisim project miscsim.circ as structural Verilog: 6 circuits, main circuit main
module main (
);

  wire and_1_out, and_2_out, CLK, controller_1_bcs, controller_1_bnz, controller_1_ld, controller_1_st,
       decoder_1_out0, decoder_1_out1, displaydecoder_1_sign, displaydecoder_2_sign, multiplexer_3_out,
       nor_1_out, not_1_out, or_1_out, xor_1_out;
  wire [1:0] alu_1_zflag, controller_1_op, controller_1_rd, controller_1_rm, controller_1_rn, register_2_q;
  wire [2:0] rom_1_data_2;
  wire [3:0] controller_1_aluop, displaydecoder_1_hundreds, displaydecoder_1_ones, displaydecoder_1_tens,
       displaydecoder_2_hundreds, displaydecoder_2_ones, displaydecoder_2_tens;
  wire [7:0] alu_1_rd, controller_1_imm, DM_dout, multiplexer_2_out, register_3_q, register_4_q,
       registerfile_1_rdd, registerfile_1_rdm, registerfile_1_rdn;
  wire [8:0] rom_1_data;
  wire [12:0] adder_1_out, adder_2_out, bit_extender_1_out, multiplexer_1_out, register_1_q;

  Multiplexer #(.width(13)) multiplexer_1 (
    .in0(adder_2_out), .in1(adder_1_out), .out(multiplexer_1_out), .sel(or_1_out));
  Clock clock_1 (.out(CLK));
  assign bit_extender_1_out = {{4{rom_1_data[8]}}, rom_1_data};  // Bit_Extender bit_extender_1
  Adder #(.width(13)) adder_1 (.a(bit_extender_1_out), .b(register_1_q), .out(adder_1_out));  // open: cin, cout
  Adder #(.width(13)) adder_2 (.a(register_1_q), .b(13'h1), .out(adder_2_out));  // open: cin, cout
  Register #(.width(13)) register_1 (.D(multiplexer_1_out), .clk(CLK), .Q(register_1_q));  // open: en, clr
  ROM #(.addrWidth(13), .dataWidth(12)) rom_1 (.addr(register_1_q), .data({rom_1_data_2, rom_1_data}));
  or or_1 (or_1_out, controller_1_bcs, controller_1_bnz);
  Controller controller_1 (
    .Din({rom_1_data_2, rom_1_data}), .ZFlag(register_2_q[0]), .CFlag(register_2_q[1]), .Rd(controller_1_rd),
    .Rm(controller_1_rm), .Rn(controller_1_rn), .ALUOP(controller_1_aluop), .OP(controller_1_op),
    .Imm(controller_1_imm), .LD(controller_1_ld), .ST(controller_1_st), .BNZ(controller_1_bnz),
    .BCS(controller_1_bcs));
  Multiplexer #(.disabled("Z"), .select(2), .width(8)) multiplexer_2 (
    .in0(alu_1_rd), .in1(registerfile_1_rdn), .in3(controller_1_imm), .out(multiplexer_2_out),
    .sel(controller_1_op));  // open: in2
  xor xor_1 (xor_1_out, controller_1_op[0], controller_1_op[1]);
  nor nor_1 (nor_1_out, xor_1_out, controller_1_st);
  RegisterFile registerfile_1 (
    .En(nor_1_out), .WAn(controller_1_rd), .RAn(controller_1_rn), .RAm(controller_1_rm),
    .WDn(multiplexer_2_out), .CLK(CLK), .Rdm(registerfile_1_rdm), .Rdd(registerfile_1_rdd),
    .Rdn(registerfile_1_rdn));
  Register #(.width(2)) register_2 (.D(alu_1_zflag), .clk(CLK), .Q(register_2_q));  // open: en, clr
  ALU alu_1 (
    .ALUOP(controller_1_aluop), .Rn(registerfile_1_rdn), .Rm(registerfile_1_rdm), .LD(DM_dout),
    .CFlag(alu_1_zflag[1]), .Rd(alu_1_rd), .ZFlag(alu_1_zflag[0]));
  and and_1 (and_1_out, controller_1_st, registerfile_1_rdn[7], registerfile_1_rdn[6], registerfile_1_rdn[5], registerfile_1_rdn[4]);
  Multiplexer multiplexer_3 (.in0(controller_1_st), .in1(not_1_out), .out(multiplexer_3_out), .sel(and_1_out));
  not not_1 (not_1_out, controller_1_st);
  and and_2 (and_2_out, and_1_out, ~registerfile_1_rdn[3], ~registerfile_1_rdn[2], ~registerfile_1_rdn[1]);  // AND_Gate
  Decoder decoder_1 (.out0(decoder_1_out0), .out1(decoder_1_out1), .sel(registerfile_1_rdn[0]), .en(and_2_out));
  RAM #(.asyncread("true"), .\type ("nonvolatile")) DM (
    .addr(registerfile_1_rdn), .we(multiplexer_3_out), .oe(controller_1_ld), .clk(CLK),
    .din(registerfile_1_rdd), .dout(DM_dout));
  Register register_3 (.D(registerfile_1_rdd), .en(decoder_1_out0), .clk(CLK), .Q(register_3_q));  // open: clr
  Register register_4 (.D(registerfile_1_rdd), .en(decoder_1_out1), .clk(CLK), .Q(register_4_q));  // open: clr
  DisplayDecoder displaydecoder_1 (
    .Din(register_3_q), .Hundreds(displaydecoder_1_hundreds), .Tens(displaydecoder_1_tens),
    .Ones(displaydecoder_1_ones), .Sign(displaydecoder_1_sign));
  DisplayDecoder displaydecoder_2 (
    .Din(register_4_q), .Hundreds(displaydecoder_2_hundreds), .Tens(displaydecoder_2_tens),
    .Ones(displaydecoder_2_ones), .Sign(displaydecoder_2_sign));
  _7_Segment_Display u_7_segment_display_1 (.g(displaydecoder_1_sign));  // open: f, a, b, e, d, c, dp
  // _7_Segment_Display 7_segment_display_2: pin names not known; wires that end beside it: displaydecoder_1_hundreds, displaydecoder_1_tens
  // BCD_to_7_Segment_decoder bcd_to_7_segment_decoder_1: pin names not known
  // BCD_to_7_Segment_decoder bcd_to_7_segment_decoder_2: pin names not known
  _7_Segment_Display u_7_segment_display_3 (.g(displaydecoder_2_sign));  // open: f, a, b, e, d, c, dp
  // _7_Segment_Display 7_segment_display_4: pin names not known; wires that end beside it: displaydecoder_2_hundreds, displaydecoder_2_tens
  // BCD_to_7_Segment_decoder bcd_to_7_segment_decoder_3: pin names not known
  // BCD_to_7_Segment_decoder bcd_to_7_segment_decoder_4: pin names not known
  // _7_Segment_Display 7_segment_display_5: pin names not known; wires that end beside it: displaydecoder_1_tens, displaydecoder_1_ones
  // BCD_to_7_Segment_decoder bcd_to_7_segment_decoder_5: pin names not known
  // _7_Segment_Display 7_segment_display_6: pin names not known; wires that end beside it: displaydecoder_2_tens, displaydecoder_2_ones
  // BCD_to_7_Segment_decoder bcd_to_7_segment_decoder_6: pin names not known
  _7_Segment_Display u_7_segment_display_7 ();  // open: g, f, a, b, e, d, c, dp
  // BCD_to_7_Segment_decoder bcd_to_7_segment_decoder_7: pin names not known
  _7_Segment_Display u_7_segment_display_8 ();  // open: g, f, a, b, e, d, c, dp
  // BCD_to_7_Segment_decoder bcd_to_7_segment_decoder_8: pin names not known

  // Notes on the sheet:
  //   PC
  //   contents of rom_1 (hex, n*v repeats v):
  //   c07 fbc 310 fbc 1d 310 fc0 1d 310 fc0 1d 310 fc4 1d 310 fc4 1d 310 fc8 1d 310 fcc 1d 310 fcc 1d 310
  //   fd0 1d 310 fd0 1d 310 fd4 1d 310 fd4 1d 310 fc8 1d 310 fc8 1d 310 fdc 1d 310 fe0 1d 310 fe0 1d 310
  //   fe4 1d 310 fe4 1d 310 fe8 1d 310 fe8 1d 310 fec 1d 310 fec 1d 310 ff0 1d 310 ff4 1d 310 ff4 1d 310
  //   ff8 1d 310 ff8 1d 310 ffc 1d 310 ffc 1d 310 c00 1d 310 c00 1d 310 c00 1d 310 c04 1d 310 c04 1d 310
  //   c08 1d 310 c08 1d 310 c0c 1d 310 c0c 1d 310 c10 1d 310 c14 1d 310 c14 1d 310 c18 1d 310 c18 1d 310
  //   c1c 1d 310 c1c 1d 310 c20 1d 310 c20 1d 310 c24 1d 310 c28 1d 310 c28 1d 310 c2c 1d 310 c2c 1d 310
  //   c30 1d 310 c30 1d 310 c34 1d 310 c34 1d 310 c38 1d 310 c3c 1d 310 c3c 1d 310 c40 1d 310 c40 1d 310
  //   c44 1d 310 c44 1d 310 c48 1d 310 c48 1d 310 c4c 1d 310 c50 1d 310 c50 1d 310 c54 1d 310 c54 1d 310
  //   c58 1d 310 c58 1d 310 c5c 1d 310 c5c 1d 310 c60 1d 310 c64 1d 310 c64 1d 310 c68 1d 310 c68 1d 310
  //   c6c 1d 310 c6c 1d 310 c70 1d 310 c70 1d 310 c74 1d 310 c78 1d 310 c78 1d 310 c7c 1d 310 c7c 1d 310
  //   c80 1d 310 c80 1d 310 c84 1d 310 c84 1d 310 c88 1d 310 c8c 1d 310 c8c 1d 310 c90 1d 310 c90 1d 310
  //   c94 1d 310 c94 1d 310 c98 1d 310 c98 1d 310 c9c 1d 310 ca0 1d 310 ca0 1d 310 ca4 1d 310 ca4 1d 310
  //   ca8 1d 310 ca8 1d 310 cac 1d 310 cac 1d 310 cb0 1d 310 cb4 1d 310 cb4 1d 310 cb8 1d 310 cb8 1d 310
  //   cbc 1d 310 cbc 1d 310 cc0 1d 310 cc0 1d 310 cc4 1d 310 cc8 1d 310 cc8 1d 310 ccc 1d 310 ccc 1d 310
  //   cd0 1d 310 cd0 1d 310 ea0 1d 310 ea0 1d 310 ea4 1d 310 ea4 1d 310 ea8 1d 310 ea8 1d 310 eac 1d 310
  //   eac 1d 310 eb0 1d 310 eb4 1d 310 eb4 1d 310 eb8 1d 310 eb8 1d 310 ebc 1d 310 ebc 1d 310 ec0 1d 310
  //   ec0 1d 310 ec4 1d 310 ec8 1d 310 ec8 1d 310 ecc 1d 310 ecc 1d 310 ed0 1d 310 ed0 1d 310 ed4 1d 310
  //   ed4 1d 310 ed8 1d 310 edc 1d 310 edc 1d 310 ee0 1d 310 ee0 1d 310 ee4 1d 310 ee4 1d 310 ee8 1d 310
  //   ee8 1d 310 eec 1d 310 ef0 1d 310 ef0 1d 310 ef4 1d 310 ef4 1d 310 ef8 1d 310 ef8 1d 310 efc 1d 310
  //   efc 1d 310 f00 1d 310 f04 1d 310 f04 1d 310 f08 1d 310 f08 1d 310 f0c 1d 310 f0c 1d 310 f10 1d 310
  //   f10 1d 310 f14 1d 310 f18 1d 310 f18 1d 310 f1c 1d 310 f1c 1d 310 f20 1d 310 f20 1d 310 f24 1d 310
  //   f24 1d 310 f28 1d 310 f2c 1d 310 f2c 1d 310 f30 1d 310 f30 1d 310 f34 1d 310 f34 1d 310 f38 1d 310
  //   f38 1d 310 f3c 1d 310 f40 1d 310 f40 1d 310 f44 1d 310 f44 1d 310 f48 1d 310 f48 1d 310 f4c 1d 310
  //   f4c 1d 310 f50 1d 310 f54 1d 310 f54 1d 310 f58 1d 310 f58 1d 310 f5c 1d 310 f5c 1d 310 f60 1d 310
  //   f60 1d 310 f64 1d 310 f68 1d 310 f68 1d 310 f6c 1d 310 f6c 1d 310 f70 1d 310 f70 1d 310 f74 1d 310
  //   f74 1d 310 f78 1d 310 f7c 1d 310 f7c 1d 310 f80 1d 310 f80 1d 310 f84 1d 310 f84 1d 310 f88 1d 310
  //   f88 1d 310 f8c 1d 310 f90 1d 310 f90 1d 310 f94 1d 310 f94 1d 310 c04 c01 c02 c03 fc2 371 323 fc6
  //   321 f 7fa
  //   Status Reg
  //   F0
  //   F1
  //   Fareinheit
  //   Celsius
endmodule

module CLA (
  input  [3:0] A,
  input  [3:0] B,
  input  Carry,
  output C4,
  output [3:0] S
);

  wire and_1_out, and_2_out, and_3_out, and_4_out, and_5_out, and_6_out, and_7_out, and_8_out, and_9_out,
       and_10_out, C1_out, C2_out, C3_out, G0_out, G1_out, G2_out, G3_out, P0_out, P1_out, P2_out, P3_out;

  xor P3 (P3_out, A[3], B[3]);
  and G3 (G3_out, A[3], B[3]);
  xor P2 (P2_out, A[2], B[2]);
  and G2 (G2_out, A[2], B[2]);
  xor P1 (P1_out, A[1], B[1]);
  and G1 (G1_out, A[1], B[1]);
  xor P0 (P0_out, A[0], B[0]);
  and G0 (G0_out, A[0], B[0]);
  and and_1 (and_1_out, Carry, P0_out, P1_out, P2_out, P3_out);
  and and_2 (and_2_out, G0_out, P1_out, P2_out, P3_out);
  and and_3 (and_3_out, G1_out, P2_out, P3_out);
  and and_4 (and_4_out, P3_out, G2_out);
  and and_5 (and_5_out, Carry, P0_out, P1_out, P2_out);
  and and_6 (and_6_out, G0_out, P1_out, P2_out);
  and and_7 (and_7_out, P2_out, G1_out);
  and and_8 (and_8_out, Carry, P0_out, P1_out);
  and and_9 (and_9_out, G0_out, P1_out);
  and and_10 (and_10_out, Carry, P0_out);
  or or_1 (C4, and_1_out, and_2_out, and_3_out, and_4_out, G3_out);
  or C3 (C3_out, and_5_out, and_6_out, and_7_out, G2_out);
  or C2 (C2_out, and_8_out, and_9_out, G1_out);
  or C1 (C1_out, and_10_out, G0_out);
  xor S3 (S[3], P3_out, C3_out);
  xor S2 (S[2], P2_out, C2_out);
  xor S1 (S[1], P1_out, C1_out);
  xor S0 (S[0], P0_out, Carry);
endmodule

module RegisterFile (
  input  En,
  input  [1:0] WAn,
  input  [1:0] RAn,
  input  [1:0] RAm,
  input  [7:0] WDn,
  input  CLK,
  output [7:0] Rdn,
  output [7:0] Rdm,
  output [7:0] Rdd
);

  wire decoder_1_out0, decoder_1_out1, decoder_1_out2, decoder_1_out3;
  wire [7:0] register_1_q, register_2_q, register_3_q, register_4_q;

  Decoder #(.select(2)) decoder_1 (
    .out0(decoder_1_out0), .out1(decoder_1_out1), .out2(decoder_1_out2), .out3(decoder_1_out3), .sel(WAn),
    .en(En));
  Register register_1 (.D(WDn), .en(decoder_1_out0), .clk(CLK), .Q(register_1_q));  // open: clr
  Register register_2 (.D(WDn), .en(decoder_1_out1), .clk(CLK), .Q(register_2_q));  // open: clr
  Register register_3 (.D(WDn), .en(decoder_1_out2), .clk(CLK), .Q(register_3_q));  // open: clr
  Register register_4 (.D(WDn), .en(decoder_1_out3), .clk(CLK), .Q(register_4_q));  // open: clr
  Multiplexer #(.select(2), .width(8)) multiplexer_1 (
    .in0(register_1_q), .in1(register_2_q), .in2(register_3_q), .in3(register_4_q), .out(Rdn), .sel(RAn));
  Multiplexer #(.select(2), .width(8)) multiplexer_2 (
    .in0(register_1_q), .in1(register_2_q), .in2(register_3_q), .in3(register_4_q), .out(Rdm), .sel(RAm));
  Multiplexer #(.disabled("Z"), .select(2), .width(8)) multiplexer_3 (
    .in0(register_1_q), .in1(register_2_q), .in2(register_3_q), .in3(register_4_q), .out(Rdd), .sel(WAn));
endmodule

module Controller (
  input  [11:0] Din,
  input  ZFlag,
  input  CFlag,
  output [1:0] Rd,
  output [1:0] Rm,
  output [1:0] Rn,
  output [3:0] ALUOP,
  output [1:0] OP,
  output [7:0] Imm,
  output LD,
  output ST,
  output BNZ,
  output BCS
);

  wire and_1_out, and_2_out;

  and and_1 (and_1_out, Din[10], ~Din[11]);  // AND_Gate
  and and_2 (and_2_out, ~Din[10], Din[11]);  // AND_Gate
  and and_3 (ST, ~Din[10], ~Din[11], Din[9], Din[8], ~Din[7], ~Din[6]);  // AND_Gate
  and and_4 (BNZ, and_1_out, ~ZFlag);  // AND_Gate
  and and_5 (BCS, CFlag, and_2_out);
  and and_6 (LD, Din[6], ~Din[7], Din[8], Din[9], ~Din[10], ~Din[11]);  // AND_Gate

  assign ALUOP = Din[9:6];
  assign Imm = Din[9:2];
  assign OP = Din[11:10];
  assign Rd = Din[1:0];
  assign Rm = Din[3:2];
  assign Rn = Din[5:4];
endmodule

module ALU (
  input  [3:0] ALUOP,
  input  [7:0] Rn,
  input  [7:0] Rm,
  input  [7:0] LD,
  output CFlag,
  output [7:0] Rd,
  output ZFlag
);

  wire and_2_out, and_3_out, cla_1_c4, cla_2_c4, or_2_out;
  wire [3:0] cla_1_s, cla_2_s;
  wire [7:0] and_1_out, multiplexer_1_out, not_1_out, not_2_out, or_1_out;

  Multiplexer #(.width(8)) multiplexer_1 (.in0(Rm), .in1(not_1_out), .out(multiplexer_1_out), .sel(ALUOP[0]));
  assign not_1_out = ~Rm;  // NOT_Gate not_1, 8 bits wide
  assign and_1_out = Rn & Rm;  // AND_Gate and_1, 8 bits wide
  assign or_1_out = Rn | Rm;  // OR_Gate or_1, 8 bits wide
  assign not_2_out = ~Rn;  // NOT_Gate not_2, 8 bits wide
  CLA cla_1 (.A(Rn[3:0]), .B(multiplexer_1_out[3:0]), .Carry(ALUOP[0]), .C4(cla_1_c4), .S(cla_1_s));
  CLA cla_2 (.A(Rn[7:4]), .B(multiplexer_1_out[7:4]), .Carry(cla_1_c4), .C4(cla_2_c4), .S(cla_2_s));
  Multiplexer #(.select(4), .width(8)) multiplexer_2 (
    .in0({cla_2_s, cla_1_s}), .in1({cla_2_s, cla_1_s}), .in2(and_1_out), .in3(or_1_out), .in4(not_2_out),
    .in5({Rn[6:0], 1'b0}), .in6({{2{Rn[7]}}, Rn[6:1]}), .in8(Rn), .in13(LD), .out(Rd), .sel(ALUOP));  // open: in7, in9, in10, in11, in12, in14, in15
  nor nor_1 (ZFlag, Rd[7], Rd[6], Rd[5], Rd[4], Rd[3], Rd[2], Rd[1], Rd[0]);
  and and_2 (and_2_out, ~ALUOP[0], ~ALUOP[1], ~ALUOP[2], ~ALUOP[3]);  // AND_Gate
  or or_2 (or_2_out, and_2_out, and_3_out);
  and and_3 (and_3_out, ALUOP[0], ~ALUOP[1], ~ALUOP[2], ~ALUOP[3]);  // AND_Gate
  and and_4 (CFlag, cla_2_c4, or_2_out);

  // Notes on the sheet:
  //   ADD/SUB
  //   OR
  //   NOT
  //   SL
  //   ASR
  //   MOV
  //   AND
endmodule

module DisplayDecoder (
  input  [7:0] Din,
  output [3:0] Hundreds,
  output [3:0] Tens,
  output [3:0] Ones,
  output Sign
);

  wire and_1_out, and_2_out, and_3_out, and_4_out, and_5_out, and_6_out, and_7_out, and_8_out, and_9_out,
       and_10_out, and_11_out, and_12_out, and_13_out, and_14_out, and_15_out, and_16_out, and_17_out,
       and_18_out, and_19_out, and_20_out, and_21_out, and_22_out, and_23_out, and_24_out, and_25_out,
       and_26_out, and_27_out, and_28_out, cla_2_c4, not_2_out, not_3_out, not_4_out, not_5_out, not_6_out,
       not_7_out, not_8_out, or_1_out, or_2_out, or_3_out, or_4_out, or_5_out, or_6_out, or_7_out, or_8_out,
       or_9_out, or_10_out, or_11_out, or_12_out, or_13_out, or_14_out, xor_1_out, xor_2_out, xor_3_out,
       xor_4_out, xor_5_out, xor_6_out, xor_7_out, xor_8_out, xor_9_out, xor_10_out, xor_11_out, xor_12_out,
       xor_13_out, xor_14_out, xor_15_out, xor_16_out, xor_17_out, xor_18_out, xor_19_out, xor_20_out,
       xor_21_out, xor_22_out, xor_24_out, xor_25_out, xor_28_out, xor_32_out;
  wire [3:0] cla_1_s, multiplexer_1_out, multiplexer_1_out_2, undriven, undriven_2;
  wire [3:1] cla_2_s;
  wire [7:0] not_1_out;

  CLA cla_1 (.A(multiplexer_1_out_2), .B(undriven), .Carry(cla_2_c4), .S(cla_1_s));  // open: C4
  CLA cla_2 (.A(multiplexer_1_out), .B(undriven_2), .Carry(Din[7]), .C4(cla_2_c4), .S({cla_2_s, Ones[0]}));
  Multiplexer #(.width(8)) multiplexer_1 (
    .in0(Din), .in1(not_1_out), .out({multiplexer_1_out_2, multiplexer_1_out}), .sel(Din[7]));
  assign not_1_out = ~Din;  // NOT_Gate not_1, 8 bits wide
  or or_1 (or_1_out, cla_1_s[2], cla_1_s[1]);
  or or_2 (or_2_out, 1'b0, and_1_out);
  and and_1 (and_1_out, cla_1_s[3], or_1_out);
  and and_2 (and_2_out, or_2_out, xor_1_out);
  xor xor_1 (xor_1_out, or_2_out, cla_1_s[1]);
  not not_2 (not_2_out, cla_1_s[2]);
  and and_3 (and_3_out, not_2_out, and_2_out);
  xor xor_2 (xor_2_out, or_2_out, and_3_out);
  xor xor_3 (xor_3_out, 1'b0, and_4_out);
  and and_4 (and_4_out, cla_1_s[3], xor_2_out);
  xor xor_4 (xor_4_out, cla_1_s[3], xor_2_out);
  xor xor_5 (xor_5_out, and_2_out, cla_1_s[2]);
  or or_3 (or_3_out, xor_1_out, cla_1_s[0]);
  and and_5 (and_5_out, xor_5_out, or_3_out);
  or or_4 (or_4_out, xor_4_out, and_5_out);
  xor xor_6 (xor_6_out, or_4_out, cla_1_s[0]);
  and and_6 (and_6_out, or_4_out, xor_6_out);
  not not_3 (not_3_out, xor_1_out);
  and and_7 (and_7_out, not_3_out, and_6_out);
  xor xor_7 (xor_7_out, or_4_out, and_7_out);
  and and_8 (and_8_out, xor_5_out, xor_7_out);
  xor xor_8 (xor_8_out, xor_4_out, and_8_out);
  xor xor_9 (xor_9_out, xor_5_out, xor_7_out);
  xor xor_10 (xor_10_out, and_6_out, xor_1_out);
  or or_5 (or_5_out, xor_6_out, cla_2_s[3]);
  and and_9 (and_9_out, xor_10_out, or_5_out);
  or or_6 (or_6_out, xor_9_out, and_9_out);
  xor xor_11 (xor_11_out, or_6_out, cla_2_s[3]);
  not not_4 (not_4_out, xor_6_out);
  and and_10 (and_10_out, or_6_out, xor_11_out);
  and and_11 (and_11_out, not_4_out, and_10_out);
  xor xor_12 (xor_12_out, or_6_out, and_11_out);
  and and_12 (and_12_out, xor_10_out, xor_12_out);
  xor xor_13 (xor_13_out, xor_9_out, and_12_out);
  xor xor_14 (xor_14_out, xor_10_out, xor_12_out);
  xor xor_15 (xor_15_out, and_10_out, xor_6_out);
  or or_7 (or_7_out, xor_11_out, cla_2_s[2]);
  or or_8 (or_8_out, xor_8_out, xor_13_out);
  and and_13 (and_13_out, xor_15_out, or_7_out);
  and and_14 (and_14_out, xor_3_out, or_8_out);
  or or_9 (or_9_out, xor_14_out, and_13_out);
  or or_10 (or_10_out, 1'b0, and_14_out);
  and and_15 (and_15_out, or_9_out, xor_16_out);
  xor xor_16 (xor_16_out, or_9_out, cla_2_s[2]);
  xor xor_17 (xor_17_out, or_10_out, xor_13_out);
  not not_5 (not_5_out, xor_11_out);
  and and_16 (and_16_out, or_10_out, xor_17_out);
  and and_17 (and_17_out, not_5_out, and_15_out);
  not not_6 (not_6_out, xor_8_out);
  and and_18 (and_18_out, not_6_out, and_16_out);
  xor xor_18 (xor_18_out, or_9_out, and_17_out);
  xor xor_19 (xor_19_out, or_10_out, and_18_out);
  and and_19 (and_19_out, xor_15_out, xor_18_out);
  xor xor_20 (xor_20_out, xor_15_out, xor_18_out);
  xor xor_21 (xor_21_out, and_15_out, xor_11_out);
  and and_20 (and_20_out, xor_3_out, xor_19_out);
  xor xor_22 (xor_22_out, xor_14_out, and_19_out);
  xor xor_23 (Hundreds[1], 1'b0, and_20_out);
  xor xor_24 (xor_24_out, xor_3_out, xor_19_out);
  xor xor_25 (xor_25_out, and_16_out, xor_8_out);
  or or_11 (or_11_out, xor_16_out, cla_2_s[1]);
  or or_12 (or_12_out, xor_20_out, and_21_out);
  and and_21 (and_21_out, xor_21_out, or_11_out);
  or or_13 (or_13_out, xor_17_out, xor_22_out);
  and and_22 (and_22_out, or_12_out, Ones[1]);
  xor xor_26 (Ones[1], or_12_out, cla_2_s[1]);
  and and_23 (and_23_out, xor_25_out, or_13_out);
  not not_7 (not_7_out, xor_16_out);
  or or_14 (or_14_out, xor_24_out, and_23_out);
  and and_24 (and_24_out, not_7_out, and_22_out);
  xor xor_27 (Tens[1], or_14_out, xor_22_out);
  xor xor_28 (xor_28_out, or_12_out, and_24_out);
  not not_8 (not_8_out, xor_17_out);
  and and_25 (and_25_out, or_14_out, Tens[1]);
  and and_26 (and_26_out, not_8_out, and_25_out);
  xor xor_29 (Tens[0], xor_20_out, and_27_out);
  and and_27 (and_27_out, xor_21_out, xor_28_out);
  xor xor_30 (Ones[3], xor_21_out, xor_28_out);
  xor xor_31 (Ones[2], and_22_out, xor_16_out);
  xor xor_32 (xor_32_out, or_14_out, and_26_out);
  and and_28 (and_28_out, xor_25_out, xor_32_out);
  xor xor_33 (Hundreds[0], xor_24_out, and_28_out);
  xor xor_34 (Tens[3], xor_25_out, xor_32_out);
  xor xor_35 (Tens[2], and_25_out, xor_17_out);

  assign Hundreds[3:2] = 2'b00;
  assign Sign = Din[7];
endmodule
